# Fritzing sketch CarroRobo (saved by Fritzing 0.9.3b)

parts:
  Part2 = Arduino Uno (Rev3)  # not connected
  Part3 = Arduino Sensor Shield v5.0
  L298N1 = L298N DC motor driver
  M5 = DC Motor
  M6 = DC Motor
  hc-sr1 = hc-sr04
  M8 = DC Motor
  M9 = DC Motor
  VCC1 = 4 x AAA Battery Mount
  LED1 = LEDs [package=led10mm]
  LED2 = LEDs [package=led10mm]  # not connected
  LED3 = smd LED [color="Red (633nm)" package="0603 [SMD]"]
  LED4 = smd LED [color="Red (633nm)" package="0603 [SMD]"]
  R1 = Resistor [tolerance=±5% resistance=220 package=THT]
  R2 = Resistor [tolerance=±5% resistance=220 package=THT]
  R3 = Resistor [tolerance=±5% resistance=220 package=THT]
  R4 = Resistor [tolerance=±5% resistance=220 package=THT]  # not connected
  J1 = Piezo Speaker
  Part4 = Bluetooth HC-05 Macho

nets:
  VCC: Part3.+5V#35, Part3.+5V#103, Part3.+5V#108, Part3.+5V#110, L298N1.5V#9, hc-sr1.VCC, Part4.VCC
  N1: Part3.TX, Part4.RXD
  N2: Part3.RX, Part4.TXD
  N3: Part3.D8, hc-sr1.Trig
  N4: Part3.D9, hc-sr1.Echo
  N5: Part3.D11, J1.pin2
  N6: Part3.D13, L298N1.ENA
  GND: Part3.GND#72, Part3.GND#115, Part3.GND#120, Part3.GND#122, hc-sr1.GND, J1.pin1, Part4.GND
  N7: Part3.D1(TX), R1.Pin_0, R2.Pin_0
  N8: Part3.D2, L298N1.IN1
  N9: Part3.D3, L298N1.IN2
  N10: Part3.D4, L298N1.IN3
  N11: Part3.D5, L298N1.IN4
  N12: Part3.D6, L298N1.ENB
  N13: Part3.+5V#92, L298N1.5V#10
  N14: Part3.GND#130, LED3.cathode, LED4.cathode
  N15: Part3.pin_145, L298N1.GND, VCC1.-
  N16: Part3.pin_146, L298N1.5V#7
  N17: L298N1.OUT1, M5.pin_2, M9.pin_2
  N18: L298N1.OUT2, M5.pin_1, M9.pin_1
  N19: L298N1.OUT3, M6.pin_2, M8.pin_2
  N20: L298N1.OUT4, M6.pin_1, M8.pin_1
  N21: L298N1.12V, VCC1.+
  N22: LED1.C, R3.Pin_1

custom parts:
  L298N DC motor driver: 2x DC motor driver with 78M05 positive voltage regulator (7..35 V) L298N: max 46 V, 2 A Set 5 V Enable jumper to enable 5 V regultor (needed for the L298N) and +5 V output at screw terminal or supply external +5 V at screw terminal Set ENA and/or ENB to +5 V to enable motor permanently or supply ENA and/or ENB with PWM signal IN1 and IN2 set rotation directory for motor A (OUT1/OUT2) IN2 and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
